// Logisim project cpu.circ as structural Verilog: 1 circuit, main circuit cpu
module cpu (
  input  clk,
  input  [31:0] INSTRUCTION,
  input  [31:0] MEM_READ_DATA,
  output [31:0] MEM_WRITE_ADDRESS,
  output [31:0] PROGRAM_COUNTER,
  output [31:0] ra,
  output [31:0] sp,
  output [31:0] t0,
  output [31:0] t1,
  output [31:0] t2,
  output [31:0] s0,
  output [31:0] s1,
  output [31:0] a0,
  output [31:0] tohost,
  output [3:0] MEM_WRITE_ENABLE,
  output [31:0] MEM_WRITE_DATA
);

  wire csrwen, regwen;
  wire [2:0] immsel;
  wire [3:0] alusel;
  wire [31:0] adder_1_out, imm, valA, valB, valC;

  Adder #(.width(32)) adder_1 (.a(PROGRAM_COUNTER), .b(32'h4), .out(adder_1_out));  // open: cin, cout
  Register #(.width(32)) PC (.D(adder_1_out), .clk(clk), .Q(PROGRAM_COUNTER));  // open: en, clr
  imm_gen imm_gen_1 (.inst(INSTRUCTION), .ImmSel(3'b000), .imm(imm));
  control_logic control_logic_1 (
    .CSRWen(csrwen), .RegWEn(regwen), .ImmSel(immsel), .ALUSel(alusel), .inst(INSTRUCTION));  // open: PCSel, BrUn, ASel, BSel, MemRW, WBSel, CSRSel, BrEq, BrLt
  // branch_comp branch_comp_1: pin names not known; wires that end beside it: csrwen
  regfile regfile_1 (
    .rs1(INSTRUCTION[19:15]), .rs2({5{1'b0}}), .rd(INSTRUCTION[11:7]), .Write_Data(valC), .RegWEn(1'b1),
    .clk(clk), .ra(ra), .sp(sp), .t0(t0), .t1(t1), .t2(t2), .s0(s0), .s1(s1), .a0(a0), .Read_Data_1(valA),
    .Read_Data_2(valB));
  // csr csr_1: pin names not known; wires that end beside it: tohost
  alu alu_1 (.Result(valC), .A(valA), .B(imm), .ALUSel(4'b0000));

  // Other names for the same wires on the sheet: opcode[6:0] = INSTRUCTION[6:0]; rd[4:0] = INSTRUCTION[11:7];
  //   func3[2:0] = INSTRUCTION[14:12]; rs1[4:0] = INSTRUCTION[19:15]; tmp_imm[11:0] = INSTRUCTION[31:20]

  // Notes on the sheet:
  //   Output to IMEM
  //   IMEM (do **NOT** move this)
  //   Inputs from IMEM
  //   Inputs/Outputs for testing. Do **NOT** move these.
  //   Outputs To DMEM
  //   DMEM (do **NOT** move this)
  //   Inputs From DMEM
endmodule
