// Logisim project imm-gen.circ as structural Verilog: 1 circuit, main circuit imm_gen
module imm_gen (
  input  [31:0] inst,
  input  [2:0] ImmSel,
  output [31:0] imm
);

  wire [31:0] sra_imm, srl_imm;

  Shifter #(.shift("lr"), .width(32)) shifter_1 (.in(inst), .\dist (5'b10100), .out(srl_imm));
  Shifter #(.shift("ar"), .width(32)) shifter_2 (.in(inst), .\dist (5'b10100), .out(sra_imm));
  Multiplexer #(.enable("false"), .select(3), .width(32)) multiplexer_1 (
    .in0(sra_imm), .in1(sra_imm), .in2(sra_imm), .in3(sra_imm), .in4(sra_imm), .in5(sra_imm), .in6(sra_imm),
    .in7(sra_imm), .out(imm), .sel(ImmSel));

  // Notes on the sheet:
  //   INPUTS to your circuit
  //   DON'T CHANGE THE LOCATIONS OF THE INPUTS AND OUTPUTS!
  //   OUTPUT from your circuit
endmodule
